// Logisim project D_FF.circ as structural Verilog: 1 circuit, main circuit main
module main (
  input  D,
  output Q
);

  wire clock_1_out, multiplexer_1_out, not_1_out;

  Multiplexer multiplexer_1 (.in0(multiplexer_1_out), .in1(D), .out(multiplexer_1_out), .sel(not_1_out));
  not not_1 (not_1_out, clock_1_out);
  Clock clock_1 (.out(clock_1_out));
  Multiplexer multiplexer_2 (.in0(Q), .in1(multiplexer_1_out), .out(Q), .sel(clock_1_out));

  // Notes on the sheet:
  //   D-FF
  //   master
  //   clk
  //   slave
endmodule
