// Logisim project MUX.circ as structural Verilog: 1 circuit, main circuit main
module main (
  input  input_1,
  input  s,
  input  input_2,
  output \output 
);

  wire transmission_1_p3;

  // Transmission_Gate transmission_1: pin names not known; wires that end beside it: input_1, s, transmission_1_p3, \output 
  not not_1 (transmission_1_p3, s);
  // Transmission_Gate transmission_2: pin names not known; wires that end beside it: input_2, transmission_1_p3, s, \output 

  // Notes on the sheet:
  //   MUX
  //   s'
  //   pmos2
  //   nmos2
  //   pmos1
  //   nmos1
  //   s'
endmodule
