// Logisim project Synchronous_UpDown_Counter.circ as structural Verilog: 1 circuit, main circuit main
module main (
  input  enable,
  input  up_0_down_1,
  output A0,
  output A1,
  output A2,
  output A3
);

  wire adder_1_cout, adder_1_out, adder_2_cout, adder_2_out, adder_3_cout, adder_3_out, adder_4_out,
       and_1_out, and_2_out, clk_out, d_ff_1_qn, d_ff_2_qn, d_ff_3_qn, multiplexer_1_out, multiplexer_2_out,
       multiplexer_3_out, reset_out;

  Multiplexer multiplexer_1 (.in0(adder_3_cout), .in1(and_1_out), .out(multiplexer_1_out), .sel(up_0_down_1));
  Multiplexer multiplexer_2 (.in0(adder_1_cout), .in1(d_ff_1_qn), .out(multiplexer_2_out), .sel(up_0_down_1));
  Multiplexer multiplexer_3 (.in0(adder_2_cout), .in1(and_2_out), .out(multiplexer_3_out), .sel(up_0_down_1));
  Adder #(.width(1)) adder_1 (.a(A0), .b(enable), .out(adder_1_out), .cout(adder_1_cout));  // open: cin
  Adder #(.width(1)) adder_2 (.a(A1), .b(multiplexer_2_out), .out(adder_2_out), .cout(adder_2_cout));  // open: cin
  Adder #(.width(1)) adder_3 (.a(A2), .b(multiplexer_3_out), .out(adder_3_out), .cout(adder_3_cout));  // open: cin
  and and_1 (and_1_out, and_2_out, d_ff_3_qn);
  Adder #(.width(1)) adder_4 (.a(A3), .b(multiplexer_1_out), .out(adder_4_out));  // open: cin, cout
  and and_2 (and_2_out, d_ff_1_qn, d_ff_2_qn);
  D_Flip_Flop d_ff_1 (.D(adder_1_out), .clk(clk_out), .Q(A0), .Qn(d_ff_1_qn), .reset(reset_out));  // open: preset
  D_Flip_Flop d_ff_2 (.D(adder_2_out), .clk(clk_out), .Q(A1), .Qn(d_ff_2_qn), .reset(reset_out));  // open: preset
  D_Flip_Flop d_ff_3 (.D(adder_3_out), .clk(clk_out), .Q(A2), .Qn(d_ff_3_qn), .reset(reset_out));  // open: preset
  D_Flip_Flop d_ff_4 (.D(adder_4_out), .clk(clk_out), .Q(A3), .reset(reset_out));  // open: Qn, preset
  Clock clk (.out(clk_out));
  Button reset (.out(reset_out));

  // Notes on the sheet:
  //   Synchronous Up/Down Counter
endmodule
