// Logisim project latch.circ as structural Verilog: 1 circuit, main circuit main
module main (
  input  D,
  input  clk,
  output q
);

  Multiplexer multiplexer_1 (.in0(q), .in1(D), .out(q), .sel(clk));

  // Notes on the sheet:
  //   Latch
endmodule
